# Fritzing sketch diagram (saved by Fritzing 0.9.3b)

parts:
  Part1 = Arduino Nano (Rev3.0)
  Part2 = Real Time Clock Module - DS1307 RTC Breakout Board

nets:
  GND: Part1.GND, Part2.GND
  N1: Part1.A5, Part2.SCL
  N2: Part1.A4, Part2.SDA
  3V3: Part1.3V3, Part2.5V

notes:
  JeVois 4-pin Serial
  Red Black White Yellow
  5050 LED
  VCC G DIN
